# Fritzing sketch RPI-UV-Meter (saved by Fritzing 1.0.2b)
breadboards: 1

parts:
  part = Raspberry Pi Zero [part_number=W]
  Part1 = Adafruit VEML6075 UV Sensor Breakout [part_number=VEML6075]
  Blu = Round Pushbutton
  Wht = Round Pushbutton
  Grn = Round Pushbutton
  Red = Round Pushbutton
  part_2 = POT [knob_status=50% power=0.5W package=pot_mammoth]
  part_3 = Resistor [tolerance=±5% power=0.25W resistance=220 package=THT]
  part_4 = Resistor [tolerance=±5% power=0.25W resistance=220 package=THT]
  part_5 = Resistor [tolerance=±5% power=0.25W resistance=10k package=THT]
  part_6 = Resistor [tolerance=±5% power=0.25W resistance=220 package=THT]
  part_7 = Resistor [tolerance=±5% power=0.25W resistance=10k package=THT]
  part_8 = Resistor [tolerance=±5% power=0.25W resistance=10k package=THT]
  part_9 = Resistor [tolerance=±5% power=0.25W resistance=10k package=THT]
  Active_Buzzer = Buzzer 12mm [part_number=COM-07950 package=buzzer-12mm-ns]
  part_10 = smd LED [color="Green (560nm)" package="1206 [SMD]"]
  part_11 = smd LED [color="Yellow (595nm)" package="1206 [SMD]"]
  part_12 = smd LED [color="Red (660nm)" package="1206 [SMD]"]
  part_13 = LCM1602 IIC [part_number="LCM1602 IIC V1" chip_label="LCM1602 IIC V1" package="DIP (Dual Inline) [THT]"]
  A1 = 2 channel relay module [package=THT]
  part_14 = LCD screen [part_number="16x2 LCD" mpn=s mn=s]

nets:
  N1: part.pin_1, Part1.3.3V
  N2: part.pin_2, part.pin_4, part_13.VCC, A1.pin_13
  N3: part.pin_3, Part1.SDA, part_13.SDA
  N4: part.pin_5, Part1.SCL, part_13.SCL
  GND: part.pin_6, part.pin_9, part.pin_34, part.pin_39, Part1.GND, Blu.leg0, Wht.leg0, Grn.leg0, Red.leg0, Active_Buzzer.2, part_10.anode, part_11.anode, part_12.anode, part_13.GND, A1.pin_14
  N5: part.pin_7, part_5.Pin_0
  N6: part.pin_8, A1.pin_16
  N7: part.pin_10, A1.pin_15
  N8: part.pin_11, part_7.Pin_1
  N9: part.pin_13, part_8.Pin_1
  N10: part.pin_15, part_9.Pin_1
  N11: part.pin_36, part_3.Pin_1
  N12: part.pin_37, part_2.E
  N13: part.pin_38, part_6.Pin_1
  N14: part.pin_40, part_4.Pin_1
  N15: Blu.leg1, part_9.Pin_0
  N16: Wht.leg1, part_8.Pin_0
  N17: Grn.leg1, part_7.Pin_0
  N18: Red.leg1, part_5.Pin_1
  N19: part_2.S, Active_Buzzer.1
  N20: part_3.Pin_0, part_10.cathode
  N21: part_4.Pin_0, part_12.cathode
  N22: part_6.Pin_0, part_11.cathode
  VSS: part_13.VSS, part_14.VSS
  VDD: part_13.VDD, part_14.VDD
  N23: part_13.V0, part_14.V0
  N24: part_13.RS, part_14.RS
  N25: part_13.RW, part_14.R/W
  N26: part_13.E, part_14.E
  N27: part_13.D0, part_14.DB0
  N28: part_13.D1, part_14.DB1
  N29: part_13.D2, part_14.DB2
  N30: part_13.D3, part_14.DB3
  N31: part_13.D4, part_14.DB4
  N32: part_13.D5, part_14.DB5
  N33: part_13.D6, part_14.DB6
  N34: part_13.D7, part_14.DB7
  N35: part_13.A, part_14.LED+
  N36: part_13.K, part_14.LED-

custom parts:
  Adafruit VEML6075 UV Sensor Breakout: This little sensor is a great way to add UVA and UVB light sensing to any microcontroller project. The VEML6075 from Vishay has both true UVA and UVB band light sensors and an I2C-controlled ADC that will take readings and integrate them. The sensor also comes with calibration registers so you can easily convert the UVA/UVB readings into the UV Index. Compared to our other UV sensors, this one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
  Round Pushbutton: A generic pushbutton.
  Buzzer 12mm: Buzzer 12mm Spark Fun Electronics SKU : Comp-Buzzer Through hole This is a small 12mm round speaker that operates around the audible 2kHz range. You can use these speakers to create simple music or user interfaces. This is not a true piezoelectric speaker but behaves similarly. Instead of a piezoelectric crystal that vibrates with an electric current, this tiny speaker uses an electromagnet to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
  LCM1602 IIC: I2C-Module to use a 1602 or 2004 LCD on with the wire.h libory Serial LCD Modul
  2 channel relay module: 2 channel Relay Module 5V 12V 24V High and Low Level Trigger Relay Control With Optocoupler Two Way relays DC 5 V 12 V 24 V Volt.
